# Fritzing sketch LightSensor (saved by Fritzing 0.9.2b)
breadboards: 1

parts:
  R1 = PHOTOCELL [package=photocell]
  Composant1 = Arduino Nano (Rev3.0)
  U1 = LIPO-1000mAh [package=lipo-1000]
  R2 = Resistor [tolerance=±5% resistance=220 package="2010 [SMD]"]

nets:
  N1: R1.P$1, R2.Pin_1
  N2: R1.P$2, Composant1.3V3
  N3: Composant1.GND, Composant1.A0, U1.-, R2.Pin_0
  N4: Composant1.VIN, U1.+
